// Logisim project muxrisccore.circ as structural Verilog: 2 circuits, main circuit core
module core (
);

  wire alu_1_we, and_1_out, and_2_out, and_3_out, and_4_out, and_5_out, cart1_p29, clock_1_out, clock_5_out,
       clock_6_out, clock_8_out, clock_9_out, comparator_1_eq, comparator_2_gt, comparator_3_eq,
       comparator_4_eq, comparator_5_eq, comparator_6_eq, comparator_7_eq, comparator_8_eq, comparator_9_eq,
       comparator_10_eq, comparator_11_eq, comparator_12_eq, comparator_12_gt, comparator_12_lt,
       comparator_13_eq, comparator_13_gt, comparator_13_lt, comparator_14_eq, multiplexer_1_out, not_1_out,
       not_2_out, not_3_out, not_4_out, not_5_out, or_1_out, or_2_out, or_4_out, register_1_q, regX_p2,
       regX_p11, rgb_video_1_p1;
  wire [1:0] bitselector_13_out, bitselector_19_out;
  wire [2:0] bitselector_11_out;
  wire [3:0] bitselector_7_out, bitselector_8_out, bitselector_9_out, bitselector_10_out;
  wire [7:0] bitselector_5_out, bitselector_6_out, bitselector_12_out;
  wire [8:0] bitselector_14_out, bitselector_17_out;
  wire [15:0] bitselector_1_out, bitselector_2_out, bitselector_3_out, bitselector_4_out;
  wire [17:0] bitselector_15_out;
  wire [23:0] bitselector_16_out, bitselector_18_out, bitselector_21_out, ram1_p2;
  wire [31:0] counter_1_q;
  wire [63:0] alu_1_outx, alu_2_outx, alu_3_outx, alu_4_outx, alu_5_outx, alu_6_outx, alu_7_outx, alu_8_outx,
       cart1_p31, cart1_p32, cart1_p33, cart1_p34, cart1_p35, cart1_p36, cart1_p37, cart1_p38, cart1_p39,
       counter_2_q, multiplexer_2_out, multiplexer_5_out, multiplexer_7_out, multiplexer_9_out,
       multiplexer_11_out, multiplexer_13_out, multiplexer_15_out, multiplexer_17_out, multiplexer_18_out,
       multiplexer_19_out, multiplexer_20_out, multiplexer_21_out, multiplexer_22_out, multiplexer_23_out,
       multiplexer_24_out, multiplexer_25_out, multiplexer_26_out, multiplexer_27_out, ram1_p3, regX_p12,
       regX_p13, regX_p14, regX_p15, regX_p16, regX_p17, regX_p18, regX_p19, regX_p20, regX_p21, regX_p22,
       regX_p23, regX_p24, regX_p25, regX_p26, regX_p27, regY_p10, regY_p11, regY_p12, regY_p13, regY_p14,
       regY_p15, regY_p16, regY_p17, regZ_p10, regZ_p11, regZ_p12, regZ_p13, regZ_p14, regZ_p15, regZ_p16,
       regZ_p17, rom1_p9, rom1_p10, rom1_p11, rom1_p12, rom1_p13, rom1_p14, rom1_p15, rom1_p16;

  BitSelector #(.group(16), .width(64)) bitselector_1 (.in(multiplexer_19_out), .out(bitselector_1_out), .sel(2'b11));
  BitSelector #(.group(16), .width(64)) bitselector_2 (.in(multiplexer_19_out), .out(bitselector_2_out), .sel(2'b10));
  BitSelector #(.group(16), .width(64)) bitselector_3 (.in(multiplexer_19_out), .out(bitselector_3_out), .sel(2'b01));
  BitSelector #(.group(16), .width(64)) bitselector_4 (.in(multiplexer_19_out), .out(bitselector_4_out), .sel(2'b00));
  BitSelector #(.group(8), .width(16)) bitselector_5 (.in(bitselector_4_out), .out(bitselector_5_out), .sel(1'b1));
  BitSelector #(.group(8), .width(16)) bitselector_6 (.in(bitselector_4_out), .out(bitselector_6_out), .sel(1'b0));
  BitSelector #(.group(4)) bitselector_7 (.in(bitselector_6_out), .out(bitselector_7_out), .sel(1'b0));
  BitSelector #(.group(4)) bitselector_8 (.in(bitselector_6_out), .out(bitselector_8_out), .sel(1'b1));
  Comparator #(.mode("unsigned")) comparator_1 (
    .a(bitselector_6_out), .b(8'h70), .eq(comparator_1_eq));  // open: gt, lt
  BitSelector #(.group(4)) bitselector_9 (.in(bitselector_6_out), .out(bitselector_9_out), .sel(1'b0));
  BitSelector #(.group(4)) bitselector_10 (.in(bitselector_6_out), .out(bitselector_10_out), .sel(1'b1));
  Comparator #(.mode("unsigned"), .width(4)) comparator_2 (
    .a(bitselector_7_out), .b(4'b0000), .gt(comparator_2_gt));  // open: eq, lt
  BitSelector #(.group(3), .width(4)) bitselector_11 (.in(bitselector_8_out), .out(bitselector_11_out), .sel(1'b0));
  Comparator #(.mode("unsigned")) comparator_3 (
    .a(bitselector_6_out), .b({8{1'b0}}), .eq(comparator_3_eq));  // open: gt, lt
  Counter #(.max('hffffffff), .width(32)) counter_1 (
    .load(or_2_out), .D({32{1'b0}}), .count(comparator_3_eq), .Q(counter_1_q), .clk(clock_1_out));  // open: carry, up, clr
  Clock clock_1 (.out(clock_1_out));
  not not_1 (not_1_out, comparator_4_eq);
  Comparator #(.mode("unsigned"), .width(64)) comparator_4 (
    .a(regY_p10), .b({64{1'b0}}), .eq(comparator_4_eq));  // open: gt, lt
  Comparator #(.mode("unsigned")) comparator_5 (
    .a(bitselector_6_out), .b(8'h10), .eq(comparator_5_eq));  // open: gt, lt
  or or_1 (or_1_out, comparator_5_eq, comparator_6_eq);
  not not_2 (not_2_out, comparator_6_eq);
  Comparator #(.mode("unsigned")) comparator_6 (
    .a(bitselector_6_out), .b(8'h20), .eq(comparator_6_eq));  // open: gt, lt
  Comparator #(.mode("unsigned")) comparator_7 (
    .a(bitselector_6_out), .b(8'h30), .eq(comparator_7_eq));  // open: gt, lt
  Comparator #(.mode("unsigned")) comparator_8 (
    .a(bitselector_6_out), .b(8'h40), .eq(comparator_8_eq));  // open: gt, lt
  Comparator #(.mode("unsigned")) comparator_9 (
    .a(bitselector_6_out), .b(8'h50), .eq(comparator_9_eq));  // open: gt, lt
  Comparator #(.mode("unsigned")) comparator_10 (
    .a(bitselector_6_out), .b(8'h60), .eq(comparator_10_eq));  // open: gt, lt
  Comparator #(.mode("unsigned")) comparator_11 (
    .a(bitselector_6_out), .b(8'h80), .eq(comparator_11_eq));  // open: gt, lt
  Comparator #(.mode("unsigned"), .width(32)) comparator_12 (
    .a(counter_1_q), .b({bitselector_2_out, bitselector_3_out}), .gt(comparator_12_gt),
    .eq(comparator_12_eq), .lt(comparator_12_lt));
  BitSelector #(.group(8), .width(16)) bitselector_12 (.in(bitselector_3_out), .out(bitselector_12_out), .sel(1'b0));
  // RAM #(.addrWidth(16), .dataWidth(64), .enables("line"), .line("octo"), .misaligned("true")) regX: pin names not known; wires that end beside it: bitselector_1_out, regX_p2, regX_p2, bitselector_5_out[1], bitselector_5_out[2], bitselector_5_out[3], bitselector_5_out[4], bitselector_5_out[5], bitselector_5_out[6], bitselector_5_out[7], regX_p11, regX_p12, regX_p13, regX_p14, regX_p15, regX_p16, regX_p17, regX_p18, regX_p19, regX_p20, regX_p21, regX_p22, regX_p23, regX_p24, regX_p25, regX_p26, regX_p27
  Clock clock_2 (.out(regX_p11));
  or or_2 (or_2_out, comparator_12_gt, comparator_12_eq);
  and and_1 (and_1_out, comparator_12_lt, comparator_3_eq);
  and and_2 (and_2_out, not_1_out, or_1_out);
  Multiplexer multiplexer_1 (.in0(and_2_out), .in1(or_1_out), .out(multiplexer_1_out), .sel(not_2_out));
  or or_3 (regX_p2, comparator_7_eq, comparator_8_eq, comparator_9_eq, comparator_10_eq, comparator_1_eq, alu_1_we);
  Multiplexer #(.select(3), .width(64)) multiplexer_2 (
    .in3({{32{1'b0}}, bitselector_2_out, bitselector_3_out}),
    .in4({bitselector_2_out, bitselector_3_out, bitselector_2_out, bitselector_3_out}),
    .in5({bitselector_3_out, bitselector_3_out, bitselector_3_out, bitselector_3_out}),
    .in6({bitselector_12_out, bitselector_12_out, bitselector_12_out, bitselector_12_out, bitselector_12_out, bitselector_12_out, bitselector_12_out, bitselector_12_out}),
    .in7(multiplexer_20_out), .out(multiplexer_2_out), .sel(bitselector_11_out));  // open: in0, in1, in2
  alu alu_1 (
    .argX(regX_p20), .argY(regY_p10), .argZ(regZ_p10), .op(bitselector_9_out), .\var (bitselector_10_out),
    .outX(alu_1_outx), .we(alu_1_we));
  Multiplexer #(.width(64)) multiplexer_3 (
    .in0(multiplexer_2_out), .in1(alu_1_outx), .out(regX_p12), .sel(comparator_2_gt));
  alu alu_2 (
    .argX(regX_p21), .argY(regY_p11), .argZ(regZ_p11), .op(bitselector_9_out), .\var (bitselector_10_out),
    .outX(alu_2_outx));  // open: we
  Multiplexer #(.width(64)) multiplexer_4 (
    .in0(multiplexer_5_out), .in1(alu_2_outx), .out(regX_p13), .sel(comparator_2_gt));
  Multiplexer #(.select(3), .width(64)) multiplexer_5 (
    .in3({{32{1'b0}}, bitselector_2_out, bitselector_3_out}),
    .in4({bitselector_2_out, bitselector_3_out, bitselector_2_out, bitselector_3_out}),
    .in5({bitselector_3_out, bitselector_3_out, bitselector_3_out, bitselector_3_out}),
    .in6({bitselector_12_out, bitselector_12_out, bitselector_12_out, bitselector_12_out, bitselector_12_out, bitselector_12_out, bitselector_12_out, bitselector_12_out}),
    .in7(multiplexer_21_out), .out(multiplexer_5_out), .sel(bitselector_11_out));  // open: in0, in1, in2
  // DualRAM #(.addrWidth(16), .dataWidth(64), .enables("line"), .line("octo"), .misaligned("true"), .\type ("nonvolatile")) regY: pin names not known; wires that end beside it: bitselector_2_out, bitselector_1_out, regX_p2, regX_p2, bitselector_5_out[1], bitselector_5_out[2], bitselector_5_out[3], bitselector_5_out[4], bitselector_5_out[5], regY_p10, regY_p11, regY_p12, regY_p13, regY_p14, regY_p15, regY_p16, regY_p17
  Clock clock_3 ();  // open: out
  Multiplexer #(.width(64)) multiplexer_6 (
    .in0(multiplexer_7_out), .in1(alu_3_outx), .out(regX_p14), .sel(comparator_2_gt));
  Multiplexer #(.select(3), .width(64)) multiplexer_7 (
    .in3({{32{1'b0}}, bitselector_2_out, bitselector_3_out}),
    .in4({bitselector_2_out, bitselector_3_out, bitselector_2_out, bitselector_3_out}),
    .in5({bitselector_3_out, bitselector_3_out, bitselector_3_out, bitselector_3_out}),
    .in6({bitselector_12_out, bitselector_12_out, bitselector_12_out, bitselector_12_out, bitselector_12_out, bitselector_12_out, bitselector_12_out, bitselector_12_out}),
    .in7(multiplexer_22_out), .out(multiplexer_7_out), .sel(bitselector_11_out));  // open: in0, in1, in2
  alu alu_3 (
    .argX(regX_p22), .argY(regY_p12), .argZ(regZ_p12), .op(bitselector_9_out), .\var (bitselector_10_out),
    .outX(alu_3_outx));  // open: we
  alu alu_4 (
    .argX(regX_p23), .argY(regY_p13), .argZ(regZ_p13), .op(bitselector_9_out), .\var (bitselector_10_out),
    .outX(alu_4_outx));  // open: we
  Multiplexer #(.width(64)) multiplexer_8 (
    .in0(multiplexer_9_out), .in1(alu_4_outx), .out(regX_p15), .sel(comparator_2_gt));
  Multiplexer #(.select(3), .width(64)) multiplexer_9 (
    .in3({{32{1'b0}}, bitselector_2_out, bitselector_3_out}),
    .in4({bitselector_2_out, bitselector_3_out, bitselector_2_out, bitselector_3_out}),
    .in5({bitselector_3_out, bitselector_3_out, bitselector_3_out, bitselector_3_out}),
    .in6({bitselector_12_out, bitselector_12_out, bitselector_12_out, bitselector_12_out, bitselector_12_out, bitselector_12_out, bitselector_12_out, bitselector_12_out}),
    .in7(multiplexer_23_out), .out(multiplexer_9_out), .sel(bitselector_11_out));  // open: in0, in1, in2
  alu alu_5 (
    .argX(regX_p24), .argY(regY_p14), .argZ(regZ_p14), .op(bitselector_9_out), .\var (bitselector_10_out),
    .outX(alu_5_outx));  // open: we
  Multiplexer #(.width(64)) multiplexer_10 (
    .in0(multiplexer_11_out), .in1(alu_5_outx), .out(regX_p16), .sel(comparator_2_gt));
  Multiplexer #(.select(3), .width(64)) multiplexer_11 (
    .in3({{32{1'b0}}, bitselector_2_out, bitselector_3_out}),
    .in4({bitselector_2_out, bitselector_3_out, bitselector_2_out, bitselector_3_out}),
    .in5({bitselector_3_out, bitselector_3_out, bitselector_3_out, bitselector_3_out}),
    .in6({bitselector_12_out, bitselector_12_out, bitselector_12_out, bitselector_12_out, bitselector_12_out, bitselector_12_out, bitselector_12_out, bitselector_12_out}),
    .in7(multiplexer_24_out), .out(multiplexer_11_out), .sel(bitselector_11_out));  // open: in0, in1, in2
  Multiplexer #(.width(64)) multiplexer_12 (
    .in0(multiplexer_13_out), .in1(alu_6_outx), .out(regX_p17), .sel(comparator_2_gt));
  Multiplexer #(.select(3), .width(64)) multiplexer_13 (
    .in3({{32{1'b0}}, bitselector_2_out, bitselector_3_out}),
    .in4({bitselector_2_out, bitselector_3_out, bitselector_2_out, bitselector_3_out}),
    .in5({bitselector_3_out, bitselector_3_out, bitselector_3_out, bitselector_3_out}),
    .in6({bitselector_12_out, bitselector_12_out, bitselector_12_out, bitselector_12_out, bitselector_12_out, bitselector_12_out, bitselector_12_out, bitselector_12_out}),
    .in7(multiplexer_25_out), .out(multiplexer_13_out), .sel(bitselector_11_out));  // open: in0, in1, in2
  alu alu_6 (
    .argX(regX_p25), .argY(regY_p15), .argZ(regZ_p15), .op(bitselector_9_out), .\var (bitselector_10_out),
    .outX(alu_6_outx));  // open: we
  // DualRAM #(.addrWidth(16), .dataWidth(64), .enables("line"), .line("octo"), .misaligned("true"), .\type ("nonvolatile")) regZ: pin names not known; wires that end beside it: bitselector_3_out, bitselector_1_out, regX_p2, regX_p2, bitselector_5_out[1], bitselector_5_out[2], bitselector_5_out[3], bitselector_5_out[4], bitselector_5_out[5], regZ_p10, regZ_p11, regZ_p12, regZ_p13, regZ_p14, regZ_p15, regZ_p16, regZ_p17
  Clock clock_4 ();  // open: out
  alu alu_7 (
    .argX(regX_p26), .argY(regY_p16), .argZ(regZ_p16), .op(bitselector_9_out), .\var (bitselector_10_out),
    .outX(alu_7_outx));  // open: we
  Multiplexer #(.width(64)) multiplexer_14 (
    .in0(multiplexer_15_out), .in1(alu_7_outx), .out(regX_p18), .sel(comparator_2_gt));
  Multiplexer #(.select(3), .width(64)) multiplexer_15 (
    .in3({{32{1'b0}}, bitselector_2_out, bitselector_3_out}),
    .in4({bitselector_2_out, bitselector_3_out, bitselector_2_out, bitselector_3_out}),
    .in5({bitselector_3_out, bitselector_3_out, bitselector_3_out, bitselector_3_out}),
    .in6({bitselector_12_out, bitselector_12_out, bitselector_12_out, bitselector_12_out, bitselector_12_out, bitselector_12_out, bitselector_12_out, bitselector_12_out}),
    .in7(multiplexer_26_out), .out(multiplexer_15_out), .sel(bitselector_11_out));  // open: in0, in1, in2
  Multiplexer #(.width(64)) multiplexer_16 (
    .in0(multiplexer_17_out), .in1(alu_8_outx), .out(regX_p19), .sel(comparator_2_gt));
  Multiplexer #(.select(3), .width(64)) multiplexer_17 (
    .in3({{32{1'b0}}, bitselector_2_out, bitselector_3_out}),
    .in4({bitselector_2_out, bitselector_3_out, bitselector_2_out, bitselector_3_out}),
    .in5({bitselector_3_out, bitselector_3_out, bitselector_3_out, bitselector_3_out}),
    .in6({bitselector_12_out, bitselector_12_out, bitselector_12_out, bitselector_12_out, bitselector_12_out, bitselector_12_out, bitselector_12_out, bitselector_12_out}),
    .in7(multiplexer_27_out), .out(multiplexer_17_out), .sel(bitselector_11_out));  // open: in0, in1, in2
  alu alu_8 (
    .argX(regX_p27), .argY(regY_p17), .argZ(regZ_p17), .op(bitselector_9_out), .\var (bitselector_10_out),
    .outX(alu_8_outx));  // open: we
  Register #(.trigger("falling"), .width(1)) register_1 (
    .D(1'b1), .en(not_3_out), .Q(register_1_q), .clk(clock_5_out));  // open: clr
  Clock clock_5 (.out(clock_5_out));
  BitSelector #(.group(2), .width(64)) bitselector_13 (.in(regY_p10), .out(bitselector_13_out), .sel({5{1'b1}}));
  BitSelector #(.group(9), .width(64)) bitselector_14 (.in(regY_p10), .out(bitselector_14_out), .sel(3'b001));
  BitSelector #(.group(18), .width(64)) bitselector_15 (.in(regY_p10), .out(bitselector_15_out), .sel(2'b00));
  Multiplexer #(.width(64)) multiplexer_18 (
    .in0(64'hc000000000000000), .in1(regX_p20), .out(multiplexer_18_out), .sel(register_1_q));
  or or_4 (or_4_out, multiplexer_1_out, not_3_out);
  not not_3 (not_3_out, register_1_q);
  and and_3 (and_3_out, comparator_11_eq, comparator_13_gt);
  Comparator #(.mode("unsigned"), .width(2)) comparator_13 (
    .a(bitselector_13_out), .b(2'b01), .gt(comparator_13_gt), .eq(comparator_13_eq), .lt(comparator_13_lt));
  BitSelector #(.group(24), .width(64)) bitselector_16 (.in(regX_p20), .out(bitselector_16_out), .sel(2'b00));
  BitSelector #(.group(9), .width(64)) bitselector_17 (.in(regY_p10), .out(bitselector_17_out), .sel(3'b000));
  not not_4 (not_4_out, and_1_out);
  Clock clock_6 (.out(clock_6_out));
  not not_5 (not_5_out, comparator_13_lt);
  // RGB_Video #(.cursor("No Cursor"), .height(512), .scale(1), .width(512)) rgb_video_1: pin names not known; wires that end beside it: rgb_video_1_p1, and_3_out, bitselector_14_out, bitselector_17_out, bitselector_16_out
  Clock clock_7 (.out(rgb_video_1_p1));
  BitSelector #(.group(24), .width(64)) bitselector_18 (.in(counter_2_q), .out(bitselector_18_out), .sel(2'b00));
  Counter #(.max('hffffffffffffffff), .trigger("falling"), .width(64)) counter_2 (
    .load(or_4_out), .D(multiplexer_18_out), .count(not_4_out), .Q(counter_2_q), .clk(clock_6_out));  // open: carry, up, clr
  and and_4 (and_4_out, comparator_13_lt, comparator_11_eq);
  and and_5 (and_5_out, comparator_13_eq, comparator_11_eq);
  RAM #(.addrWidth(18), .dataWidth(64), .enables("line")) disp1 (
    .addr(bitselector_15_out), .we(and_3_out), .clk(clock_8_out), .din(regX_p20));  // open: dout
  Clock clock_8 (.out(clock_8_out));
  BitSelector #(.group(2), .width(64)) bitselector_19 (.in(counter_2_q), .out(bitselector_19_out), .sel({5{1'b1}}));
  // DualRAM #(.addrWidth(24), .dataWidth(64), .enables("line"), .line("octo"), .misaligned("true"), .\type ("nonvolatile")) ram1: pin names not known; wires that end beside it: bitselector_18_out, ram1_p2, ram1_p3
  BitSelector #(.group(24), .width(64)) bitselector_20 (.in(regY_p10), .out(ram1_p2), .sel(2'b00));
  Clock clock_9 (.out(clock_9_out));
  BitSelector #(.group(24), .width(64)) bitselector_21 (.in(regY_p10), .out(bitselector_21_out), .sel(2'b00));
  // RAM #(.addrWidth(24), .dataWidth(64), .enables("line"), .line("octo"), .misaligned("true")) cart1: pin names not known; wires that end beside it: and_4_out, and_4_out, bitselector_5_out[1], bitselector_5_out[2], bitselector_5_out[3], bitselector_5_out[4], bitselector_5_out[5], bitselector_5_out[6], bitselector_5_out[7], clock_9_out, regX_p20, regX_p21, regX_p22, regX_p23, regX_p24, regX_p25, regX_p26, regX_p27, bitselector_21_out, and_5_out, and_5_out, bitselector_5_out[1], bitselector_5_out[2], bitselector_5_out[3], bitselector_5_out[4], bitselector_5_out[5], bitselector_5_out[6], bitselector_5_out[7], cart1_p29, regX_p20, cart1_p31, cart1_p32, cart1_p33, cart1_p34, cart1_p35, cart1_p36, cart1_p37, cart1_p38, cart1_p39
  Clock clock_10 (.out(cart1_p29));
  // ROM #(.addrWidth(24), .dataWidth(64), .line("octo"), .misaligned("true")) rom1: pin names not known; wires that end beside it: regX_p21, regX_p22, regX_p23, regX_p24, regX_p25, regX_p26, regX_p27, bitselector_18_out, rom1_p9, rom1_p10, rom1_p11, rom1_p12, rom1_p13, rom1_p14, rom1_p15, rom1_p16
  Comparator #(.mode("unsigned"), .width(2)) comparator_14 (
    .a(bitselector_19_out), .b(2'b11), .eq(comparator_14_eq));  // open: gt, lt
  Multiplexer #(.width(64)) multiplexer_19 (
    .in0(ram1_p3), .in1(rom1_p16), .out(multiplexer_19_out), .sel(comparator_14_eq));
  Multiplexer #(.width(64)) multiplexer_20 (
    .in0(cart1_p31), .in1(cart1_p39), .out(multiplexer_20_out), .sel(not_5_out));
  Multiplexer #(.width(64)) multiplexer_21 (.in0(cart1_p32), .in1(rom1_p9), .out(multiplexer_21_out), .sel(not_5_out));
  Multiplexer #(.width(64)) multiplexer_22 (.in0(cart1_p33), .in1(rom1_p10), .out(multiplexer_22_out), .sel(not_5_out));
  Multiplexer #(.width(64)) multiplexer_23 (.in0(cart1_p34), .in1(rom1_p11), .out(multiplexer_23_out), .sel(not_5_out));
  Multiplexer #(.width(64)) multiplexer_24 (.in0(cart1_p35), .in1(rom1_p12), .out(multiplexer_24_out), .sel(not_5_out));
  Multiplexer #(.width(64)) multiplexer_25 (.in0(cart1_p36), .in1(rom1_p13), .out(multiplexer_25_out), .sel(not_5_out));
  Multiplexer #(.width(64)) multiplexer_26 (.in0(cart1_p37), .in1(rom1_p14), .out(multiplexer_26_out), .sel(not_5_out));
  Multiplexer #(.width(64)) multiplexer_27 (.in0(cart1_p38), .in1(rom1_p15), .out(multiplexer_27_out), .sel(not_5_out));

  // Notes on the sheet:
  //   contents of rom1 (hex, n*v repeats v):
  //   400000000030 2000000200030 3000000080330 5000000100030 6c00000000030 a0000000f0030 b000000000030
  //   6000600020002 60006000a0072 20002 7000000000070 7000700050012 c000700000001 b000c00000020
  //   1000000030004 1000100030004 4000400030004 1000010000ff70 1000040000ff80 8000400070024 9000800000011
  //   6000900000020 b000000000010
endmodule

module alu (
  input  [63:0] argX,
  input  [63:0] argY,
  input  [63:0] argZ,
  input  [3:0] op,
  input  [3:0] \var ,
  output [63:0] outX,
  output we
);

  wire adder_1_cout, and_1_out, and_2_out, and_4_out, and_5_out, and_6_out, and_7_out, bitfinder_1_found,
       bitfinder_2_found, bitfinder_3_found, bitfinder_4_found, clock_1_out, clock_3_out, clock_4_out,
       comparator_1_eq, comparator_2_eq, comparator_2_lt, comparator_3_eq, comparator_4_eq, comparator_5_eq,
       comparator_6_eq, comparator_7_eq, comparator_8_eq, comparator_9_eq, comparator_10_eq,
       comparator_11_eq, comparator_11_lt, comparator_12_eq, comparator_13_eq, comparator_14_eq,
       comparator_15_eq, comparator_16_eq, comparator_17_eq, fpclassificator_1_p1, fpclassificator_1_p2,
       fpcomparator_1_p6, fpcomparator_1_p7, fpcomparator_2_p3, fpcomparator_2_p4, not_1_out, not_3_out,
       not_4_out, not_5_out, random_1_p1, subtractor_1_bout;
  wire [2:0] bitselector_2_out;
  wire [5:0] bitfinder_1_index, bitfinder_2_index, bitfinder_3_index, bitfinder_4_index, bitselector_1_out;
  wire [6:0] bitadder_1_out;
  wire [63:0] adder_1_out, and_3_out, bit_extender_1_out, bit_extender_2_out, bit_extender_3_out,
       bit_extender_4_out, bit_extender_5_out, bit_extender_6_out, bit_extender_7_out, bit_extender_8_out,
       bit_extender_9_out, buffer_1_out, buffer_2_out, counter_1_q, counter_2_q, divider_1_out,
       divider_1_rem, fpadder_1_out, fpdivider_1_out, fpexponentiator_1_p1, fplogarithm_1_p3,
       fpmultiplier_1_out, fpnegator_1_p2, fpsquareroot_1_p1, fpsubtractor_1_out, fptoint_1_p1, fptoint_2_p1,
       fptoint_3_p1, fptoint_4_p1, fptrigonometry_1_p4, fptrigonometry_1_p5, fptrigonometry_1_p6,
       fptrigonometry_2_p2, fptrigonometry_2_p3, fptrigonometry_2_p4, inttofp_1_p1, multiplexer_1_out,
       multiplexer_2_out, multiplexer_3_out, multiplexer_4_out, multiplexer_5_out, multiplexer_6_out,
       multiplexer_7_out, multiplexer_8_out, multiplexer_9_out, multiplexer_10_out, multiplexer_11_out,
       multiplexer_12_out, multiplexer_13_out, multiplexer_14_out, multiplexer_15_out, multiplexer_16_out,
       multiplexer_17_out, multiplexer_18_out, multiplexer_19_out, multiplexer_20_out, multiplexer_21_out,
       multiplexer_22_out, multiplier_1_cout, multiplier_1_out, nand_1_out, negator_1_out, nor_1_out,
       not_2_out, or_1_out, register_1_q, shifter_1_out, shifter_2_out, shifter_3_out, shifter_4_out,
       shifter_5_out, subtractor_1_out, undriven, xnor_1_out, xor_1_out;

  BitSelector #(.group(6), .width(64)) bitselector_1 (.in(argZ), .out(bitselector_1_out), .sel(4'b0000));
  Comparator #(.mode("unsigned"), .width(4)) comparator_1 (.a(op), .b(4'b0001), .eq(comparator_1_eq));  // open: gt, lt
  Comparator #(.width(64)) comparator_2 (
    .a(argY), .b({64{1'b0}}), .eq(comparator_2_eq), .lt(comparator_2_lt));  // open: gt
  // FPComparator #(.fpwidth(64)) fpcomparator_1: pin names not known; wires that end beside it: argX, argY, argZ, argY, {64{1'b0}}, fpcomparator_1_p6, fpcomparator_1_p7
  Comparator #(.mode("unsigned"), .width(4)) comparator_3 (.a(op), .b(4'b0010), .eq(comparator_3_eq));  // open: gt, lt
  Shifter #(.width(64)) shifter_1 (.in(argY), .\dist (bitselector_1_out), .out(shifter_1_out));
  Comparator #(.mode("unsigned"), .width(4)) comparator_4 (.a(op), .b(4'b0011), .eq(comparator_4_eq));  // open: gt, lt
  BitFinder #(.width(64)) bitfinder_1 (.in(argY), .index(bitfinder_1_index), .found(bitfinder_1_found));
  Comparator #(.mode("unsigned"), .width(4)) comparator_5 (.a(op), .b(4'b0100), .eq(comparator_5_eq));  // open: gt, lt
  Adder #(.width(64)) adder_1 (.a(argZ), .b(argY), .out(adder_1_out), .cout(adder_1_cout));  // open: cin
  assign bit_extender_1_out = {{63{1'b0}}, adder_1_cout};  // Bit_Extender bit_extender_1
  Comparator #(.mode("unsigned"), .width(4)) comparator_6 (.a(op), .b(4'b0101), .eq(comparator_6_eq));  // open: gt, lt
  FPAdder #(.fpwidth(64)) fpadder_1 (.a(argY), .b(argZ), .out(fpadder_1_out));
  Comparator #(.mode("unsigned"), .width(4)) comparator_7 (.a(op), .b(4'b0110), .eq(comparator_7_eq));  // open: gt, lt
  // FPTrigonometry #(.fpwidth(64)) fptrigonometry_1: pin names not known; wires that end beside it: argX, argY, argZ, fptrigonometry_1_p4, fptrigonometry_1_p5, fptrigonometry_1_p6
  Comparator #(.mode("unsigned"), .width(4)) comparator_8 (.a(op), .b(4'b0111), .eq(comparator_8_eq));  // open: gt, lt
  not not_1 (not_1_out, comparator_9_eq);
  Comparator #(.width(64)) comparator_9 (.a({64{1'b0}}), .b(argZ), .eq(comparator_9_eq));  // open: gt, lt
  Multiplexer #(.select(4), .width(64)) multiplexer_1 (
    .in0(multiplexer_2_out), .in1(multiplexer_10_out), .in2(multiplexer_11_out), .in3(multiplexer_12_out),
    .in4(multiplexer_14_out), .in5(multiplexer_15_out), .in6(multiplexer_16_out), .in7(multiplexer_19_out),
    .out(multiplexer_1_out), .sel(\var ));  // open: in8, in9, in10, in11, in12, in13, in14, in15
  Multiplexer #(.width(64)) multiplexer_2 (
    .in0({64{1'b0}}), .in1(64'h1), .out(multiplexer_2_out), .sel(comparator_2_eq));
  Multiplexer #(.select(4), .width(64)) multiplexer_3 (
    .in0(shifter_1_out), .in1(shifter_2_out), .in2(shifter_3_out), .in3(shifter_4_out), .in4(shifter_5_out),
    .in5(buffer_1_out), .in6(not_2_out), .in7(or_1_out), .in8(and_3_out), .in9(nand_1_out), .in10(nor_1_out),
    .in11(xor_1_out), .in12(xnor_1_out), .in13(multiplexer_20_out), .out(multiplexer_3_out), .sel(\var ));  // open: in14, in15
  Shifter #(.shift("lr"), .width(64)) shifter_2 (.in(argY), .\dist (bitselector_1_out), .out(shifter_2_out));
  Multiplexer #(.select(4), .width(64)) multiplexer_4 (
    .in0(multiplexer_5_out), .in1(multiplexer_13_out), .in2(multiplexer_17_out), .in3(multiplexer_21_out),
    .in4(bit_extender_7_out), .out(multiplexer_4_out), .sel(\var ));  // open: in5, in6, in7, in8, in9, in10, in11, in12, in13, in14, in15
  assign bit_extender_2_out = {{58{1'b0}}, bitfinder_1_index};  // Bit_Extender bit_extender_2
  Multiplexer #(.width(64)) multiplexer_5 (
    .in0({64{1'b1}}), .in1(bit_extender_2_out), .out(multiplexer_5_out), .sel(bitfinder_1_found));
  Multiplexer #(.select(4), .width(64)) multiplexer_6 (
    .in0(adder_1_out), .in1(bit_extender_1_out), .in2(subtractor_1_out), .in3(bit_extender_3_out),
    .in4(multiplier_1_out), .in5(multiplier_1_cout), .in6(divider_1_out), .in7(divider_1_rem),
    .in8(negator_1_out), .out(multiplexer_6_out), .sel(\var ));  // open: in9, in10, in11, in12, in13, in14, in15
  Subtractor #(.width(64)) subtractor_1 (
    .a(argY), .b(argZ), .out(subtractor_1_out), .bout(subtractor_1_bout));  // open: bin
  Multiplexer #(.select(4), .width(64)) multiplexer_7 (
    .in0(fpadder_1_out), .in1(fpsubtractor_1_out), .in2(fpmultiplier_1_out), .in3(fpdivider_1_out),
    .in4(fpnegator_1_p2), .in5(inttofp_1_p1), .in6(fptoint_1_p1), .in7(fptoint_2_p1), .in8(fptoint_3_p1),
    .in9(fptoint_4_p1), .in10(bit_extender_8_out), .in11(bit_extender_9_out), .out(multiplexer_7_out),
    .sel(\var ));  // open: in12, in13, in14, in15
  FPSubtractor #(.fpwidth(64)) fpsubtractor_1 (.a(argY), .b(argZ), .out(fpsubtractor_1_out));
  Multiplexer #(.select(4), .width(64)) multiplexer_8 (
    .in0(fptrigonometry_1_p4), .in1(fptrigonometry_1_p5), .in2(fptrigonometry_1_p6),
    .in3(fptrigonometry_2_p2), .in4(fptrigonometry_2_p3), .in5(fptrigonometry_2_p4), .in6(fplogarithm_1_p3),
    .in7(fpexponentiator_1_p1), .in8(fpsquareroot_1_p1), .out(multiplexer_8_out), .sel(\var ));  // open: in9, in10, in11, in12, in13, in14, in15
  // FPTrigonometry #(.fpwidth(64), .\type ("arc")) fptrigonometry_2: pin names not known; wires that end beside it: argY, fptrigonometry_2_p2, fptrigonometry_2_p3, fptrigonometry_2_p4
  Multiplexer #(.select(4), .width(64)) multiplexer_9 (
    .in0(counter_1_q), .in1(undriven), .in2(multiplexer_18_out), .in3(multiplexer_22_out), .in4(counter_2_q),
    .out(multiplexer_9_out), .sel(\var ));  // open: in5, in6, in7, in8, in9, in10, in11, in12, in13, in14, in15
  and and_1 (and_1_out, and_2_out, not_1_out);
  Clock clock_1 (.out(clock_1_out));
  Multiplexer #(.width(64)) multiplexer_10 (
    .in0({64{1'b0}}), .in1(64'h1), .out(multiplexer_10_out), .sel(comparator_2_lt));
  Multiplexer #(.width(64)) multiplexer_11 (
    .in0({64{1'b0}}), .in1(64'h1), .out(multiplexer_11_out), .sel(fpcomparator_1_p6));
  Shifter #(.shift("ar"), .width(64)) shifter_3 (.in(argY), .\dist (bitselector_1_out), .out(shifter_3_out));
  BitFinder #(.\type ("high1"), .width(64)) bitfinder_2 (
    .in(argY), .index(bitfinder_2_index), .found(bitfinder_2_found));
  assign bit_extender_3_out = {{63{1'b0}}, subtractor_1_bout};  // Bit_Extender bit_extender_3
  FPMultiplier #(.fpwidth(64)) fpmultiplier_1 (.a(argY), .b(argZ), .out(fpmultiplier_1_out));
  // FPLogarithm #(.fpwidth(64)) fplogarithm_1: pin names not known; wires that end beside it: argY, argZ, fplogarithm_1_p3, argY, argZ
  // Random #(.seed(12345667), .width(64)) random_1: pin names not known; wires that end beside it: random_1_p1
  Counter #(.max('hffffffffffffffff), .width(64)) counter_1 (
    .load(and_1_out), .D(argY), .Q(counter_1_q), .clk(clock_1_out));  // open: count, carry, up, clr
  Clock clock_2 (.out(random_1_p1));
  Multiplexer #(.width(64)) multiplexer_12 (
    .in0({64{1'b0}}), .in1(64'h1), .out(multiplexer_12_out), .sel(fpcomparator_1_p7));
  Shifter #(.shift("rl"), .width(64)) shifter_4 (.in(argY), .\dist (bitselector_1_out), .out(shifter_4_out));
  assign bit_extender_4_out = {{58{1'b0}}, bitfinder_2_index};  // Bit_Extender bit_extender_4
  Multiplier #(.mode("twosComplement"), .width(64)) multiplier_1 (
    .a(argY), .b(argZ), .out(multiplier_1_out), .cout(multiplier_1_cout));  // open: cin
  FPDivider #(.fpwidth(64)) fpdivider_1 (.a(argY), .b(argZ), .out(fpdivider_1_out));
  // FPExponentiator #(.fpwidth(64)) fpexponentiator_1: pin names not known; wires that end beside it: fpexponentiator_1_p1, argY
  Comparator #(.mode("unsigned"), .width(4)) comparator_10 (
    .a(\var ), .b(4'b0000), .eq(comparator_10_eq));  // open: gt, lt
  and and_2 (and_2_out, comparator_10_eq, comparator_8_eq);
  Comparator #(.width(64)) comparator_11 (
    .a(argY), .b(argZ), .eq(comparator_11_eq), .lt(comparator_11_lt));  // open: gt
  // FPComparator #(.fpwidth(64)) fpcomparator_2: pin names not known; wires that end beside it: argY, argZ, fpcomparator_2_p3, fpcomparator_2_p4
  assign not_2_out = ~argY;  // NOT_Gate not_2, 64 bits wide
  assign buffer_1_out = argY;  // Buffer buffer_1, 64 bits wide
  Shifter #(.shift("rr"), .width(64)) shifter_5 (.in(argY), .\dist (bitselector_1_out), .out(shifter_5_out));
  Multiplexer #(.width(64)) multiplexer_13 (
    .in0({64{1'b1}}), .in1(bit_extender_4_out), .out(multiplexer_13_out), .sel(bitfinder_2_found));
  Divider #(.mode("twosComplement"), .width(64)) divider_1 (
    .a(argY), .b(argZ), .out(divider_1_out), .rem(divider_1_rem));  // open: upper
  // FPNegator #(.fpwidth(64)) fpnegator_1: pin names not known; wires that end beside it: argY, fpnegator_1_p2, argY
  // IntToFP #(.fpwidth(64), .width(64)) inttofp_1: pin names not known; wires that end beside it: inttofp_1_p1, argY
  // FPSquareRoot #(.fpwidth(64)) fpsquareroot_1: pin names not known; wires that end beside it: fpsquareroot_1_p1
  Comparator #(.mode("unsigned"), .width(4)) comparator_12 (
    .a(\var ), .b(4'b0010), .eq(comparator_12_eq));  // open: gt, lt
  not not_3 (not_3_out, comparator_13_eq);
  Comparator #(.width(64)) comparator_13 (.a({64{1'b0}}), .b(argZ), .eq(comparator_13_eq));  // open: gt, lt
  Multiplexer #(.width(64)) multiplexer_14 (
    .in0({64{1'b0}}), .in1(64'h1), .out(multiplexer_14_out), .sel(comparator_11_eq));
  Multiplexer #(.width(64)) multiplexer_15 (
    .in0({64{1'b0}}), .in1(64'h1), .out(multiplexer_15_out), .sel(comparator_11_lt));
  assign nand_1_out = ~(argY & argZ);  // NAND_Gate nand_1, 64 bits wide
  assign or_1_out = argY | argZ;  // OR_Gate or_1, 64 bits wide
  assign and_3_out = argY & argZ;  // AND_Gate and_3, 64 bits wide
  assign bit_extender_5_out = {{58{1'b0}}, bitfinder_3_index};  // Bit_Extender bit_extender_5
  BitFinder #(.\type ("low0"), .width(64)) bitfinder_3 (
    .in(argY), .index(bitfinder_3_index), .found(bitfinder_3_found));
  Negator #(.width(64)) negator_1 (.in(argY), .out(negator_1_out));
  // FPToInt #(.fpwidth(64), .width(64)) fptoint_1: pin names not known; wires that end beside it: fptoint_1_p1, argY
  and and_4 (and_4_out, comparator_12_eq, comparator_8_eq);
  Register #(.width(64)) register_1 (.D(argY), .en(and_5_out), .clk(clock_3_out), .Q(register_1_q));  // open: clr
  and and_5 (and_5_out, and_4_out, not_3_out);
  Clock clock_3 (.out(clock_3_out));
  Multiplexer #(.width(64)) multiplexer_16 (
    .in0({64{1'b0}}), .in1(64'h1), .out(multiplexer_16_out), .sel(fpcomparator_2_p3));
  assign nor_1_out = ~(argY | argZ);  // NOR_Gate nor_1, 64 bits wide
  assign xor_1_out = argY ^ argZ;  // XOR_Gate xor_1, 64 bits wide
  Multiplexer #(.width(64)) multiplexer_17 (
    .in0({64{1'b1}}), .in1(bit_extender_5_out), .out(multiplexer_17_out), .sel(bitfinder_3_found));
  // FPToInt #(.fpwidth(64), .mode("floor"), .width(64)) fptoint_2: pin names not known; wires that end beside it: fptoint_2_p1, argY
  Multiplexer #(.width(64)) multiplexer_18 (
    .in0(register_1_q), .in1(64'h12a05f200), .out(multiplexer_18_out), .sel(comparator_14_eq));
  Comparator #(.width(64)) comparator_14 (.a({64{1'b0}}), .b(register_1_q), .eq(comparator_14_eq));  // open: gt, lt
  Multiplexer #(.width(64)) multiplexer_19 (
    .in0({64{1'b0}}), .in1(64'h1), .out(multiplexer_19_out), .sel(fpcomparator_2_p4));
  assign xnor_1_out = ~(argY ^ argZ);  // XNOR_Gate xnor_1, 64 bits wide
  BitFinder #(.\type ("high0"), .width(64)) bitfinder_4 (
    .in(argY), .index(bitfinder_4_index), .found(bitfinder_4_found));
  // FPToInt #(.fpwidth(64), .mode("ceil"), .width(64)) fptoint_3: pin names not known; wires that end beside it: fptoint_3_p1, argY
  Multiplexer #(.width(64)) multiplexer_20 (.in0(argX), .in1(buffer_2_out), .out(multiplexer_20_out), .sel(not_4_out));
  assign buffer_2_out = argY;  // Buffer buffer_2, 64 bits wide
  not not_4 (not_4_out, comparator_15_eq);
  Comparator #(.mode("unsigned"), .width(64)) comparator_15 (
    .a(argZ), .b({64{1'b0}}), .eq(comparator_15_eq));  // open: gt, lt
  assign bit_extender_6_out = {{58{1'b0}}, bitfinder_4_index};  // Bit_Extender bit_extender_6
  Multiplexer #(.width(64)) multiplexer_21 (
    .in0({64{1'b1}}), .in1(bit_extender_6_out), .out(multiplexer_21_out), .sel(bitfinder_4_found));
  // FPToInt #(.fpwidth(64), .mode("truncate"), .width(64)) fptoint_4: pin names not known; wires that end beside it: fptoint_4_p1, argY
  BitSelector #(.group(3), .width(64)) bitselector_2 (.in(argY), .out(bitselector_2_out), .sel({5{1'b0}}));
  BitAdder #(.width(64)) bitadder_1 (.in0(argY), .out(bitadder_1_out));
  // FPClassificator #(.fpwidth(64)) fpclassificator_1: pin names not known; wires that end beside it: fpclassificator_1_p1, fpclassificator_1_p2
  Multiplexer #(.select(3), .width(64)) multiplexer_22 (
    .in0({64{1'b0}}), .in1(64'h1), .in2(64'h65536), .in3(64'h1000000), .in4(64'h200), .in5(64'h200),
    .in6({64{1'b0}}), .in7({64{1'b0}}), .out(multiplexer_22_out), .sel(bitselector_2_out));
  assign bit_extender_7_out = {{57{1'b0}}, bitadder_1_out};  // Bit_Extender bit_extender_7
  assign bit_extender_8_out = {{63{1'b0}}, fpclassificator_1_p1};  // Bit_Extender bit_extender_8
  assign bit_extender_9_out = {{63{1'b0}}, fpclassificator_1_p2};  // Bit_Extender bit_extender_9
  not not_5 (not_5_out, comparator_16_eq);
  Comparator #(.width(64)) comparator_16 (.a({64{1'b0}}), .b(argZ), .eq(comparator_16_eq));  // open: gt, lt
  Comparator #(.mode("unsigned"), .width(4)) comparator_17 (
    .a(\var ), .b(4'b0100), .eq(comparator_17_eq));  // open: gt, lt
  and and_6 (and_6_out, comparator_17_eq, comparator_8_eq);
  and and_7 (and_7_out, and_6_out, not_5_out);
  Clock #(.lowDuration(9)) clock_4 (.out(clock_4_out));
  Counter #(.max('hffffffffffffffff), .width(64)) counter_2 (
    .load(and_7_out), .D(argY), .Q(counter_2_q), .clk(clock_4_out));  // open: count, carry, up, clr
  or or_2 (we, comparator_1_eq, comparator_3_eq, comparator_4_eq, comparator_5_eq, comparator_6_eq, comparator_7_eq, comparator_8_eq);
  Multiplexer #(.select(4), .width(64)) multiplexer_23 (
    .in1(multiplexer_1_out), .in2(multiplexer_3_out), .in3(multiplexer_4_out), .in4(multiplexer_6_out),
    .in5(multiplexer_7_out), .in6(multiplexer_8_out), .in7(multiplexer_9_out), .out(outX), .sel(op));  // open: in0, in8, in9, in10, in11, in12, in13, in14, in15
endmodule
